# Fritzing sketch DistanceAlerter-Arduino (saved by Fritzing 0.9.3b)
breadboards: 1

parts:
  LED1 = LED - 5mm [color="Red (633nm)" package="5 mm [THT]"]
  Speaker = KY-006 Passive Buzzer Module [package="Breakout board"]
  R1 = Resistor [tolerance=±5% resistance=220 package=THT]
  Arduino = Arduino Uno (Rev3)
  Ultrasonic_Sensor = hc-sr04

nets:
  GND: LED1.cathode, Speaker.-, Arduino.GND, Ultrasonic_Sensor.GND
  N1: LED1.anode, R1.Pin_0
  N2: Speaker.S, Arduino.D2
  N3: R1.Pin_1, Arduino.D7
  N4: Arduino.D4, Ultrasonic_Sensor.Echo
  N5: Arduino.D5_PWM, Ultrasonic_Sensor.Trig
  5V: Arduino.5V, Ultrasonic_Sensor.VCC

custom parts:
  KY-006 Passive Buzzer Module: Passive Piezoelectric Buzzer Module Keyes KY-006, it can produce a range of sound tones depending on the input frequency.
